// Logisim project ALU.circ as structural Verilog: 6 circuits, main circuit ALU
module main (
  input  [3:0] SlctOP,
  input  [7:0] Data,
  input  [2:0] in_3,
  input  [3:0] in_4,
  input  [2:0] in_5,
  output [7:0] A,
  output [7:0] B,
  output [7:0] C
);

  wire alu_1_error, registerband_8bit_1_s_1bit;

  RegisterBand_8bit registerband_8bit_1 (
    .Data(Data), .SlctA(in_3), .SlctC(in_4), .SlctB(in_5), .A(A), .B(B), .S_1bit(registerband_8bit_1_s_1bit));
  LED led_1 (.in(registerband_8bit_1_s_1bit));
  LED led_2 (.in(alu_1_error));
  ALU alu_1 (.A(A), .B(B), .SlctOP(SlctOP), .Error(alu_1_error), .C(C));
endmodule

module ALU (
  input  [7:0] A,
  input  [7:0] B,
  input  [3:0] SlctOP,
  output Error,
  output [7:0] C
);

  wire arithmetic_operation_8bit_1_error, comparator_operation_8bit_1_s, offset_rotation_8bit_1_error;
  wire [7:0] arithmetic_operation_8bit_1_s, bit_extender_1_out, logic_operation_8bit_1_s,
       offset_rotation_8bit_1_s;

  Multiplexer #(.select(4)) multiplexer_1 (
    .in0(arithmetic_operation_8bit_1_error), .in1(arithmetic_operation_8bit_1_error), .in2(1'b0), .in3(1'b0),
    .in4(1'b0), .in5(1'b0), .in6(1'b0), .in7(1'b0), .in8(1'b0), .in9(1'b0), .in10(1'b0), .in11(1'b0),
    .in12(offset_rotation_8bit_1_error), .in13(offset_rotation_8bit_1_error), .in14(1'b0), .in15(1'b0),
    .out(Error), .sel(SlctOP));
  Arithmetic_Operation_8bit arithmetic_operation_8bit_1 (
    .A(A), .B(B), .SlctOP(SlctOP), .Error(arithmetic_operation_8bit_1_error),
    .S(arithmetic_operation_8bit_1_s));
  Comparator_Operation_8bit comparator_operation_8bit_1 (
    .A(A), .B(B), .SlctOP(SlctOP), .S(comparator_operation_8bit_1_s));
  Logic_Operation_8bit logic_operation_8bit_1 (.A(A), .B(B), .SlctOP(SlctOP), .S(logic_operation_8bit_1_s));
  Offset_Rotation_8bit offset_rotation_8bit_1 (
    .A(A), .SlctOP(SlctOP), .Error(offset_rotation_8bit_1_error), .S(offset_rotation_8bit_1_s));
  assign bit_extender_1_out = {{7{1'b0}}, comparator_operation_8bit_1_s};  // Bit_Extender bit_extender_1
  Multiplexer #(.select(2), .width(8)) multiplexer_2 (
    .in0(arithmetic_operation_8bit_1_s), .in1(bit_extender_1_out), .in2(logic_operation_8bit_1_s),
    .in3(offset_rotation_8bit_1_s), .out(C), .sel(SlctOP[3:2]));
endmodule

module Arithmetic_Operation_8bit (
  input  [7:0] A,
  input  [7:0] B,
  input  [3:0] SlctOP,
  output Error,
  output [7:0] S
);

  wire add_8bits_1_overflow, substractor_8bit_1_error;
  wire [7:0] add_8bits_1_s, substractor_8bit_1_s;

  Add_8bits add_8bits_1 (.A(A), .B(B), .S(add_8bits_1_s), .Overflow(add_8bits_1_overflow));
  substractor_8bit substractor_8bit_1 (.A(A), .B(B), .Error(substractor_8bit_1_error), .S(substractor_8bit_1_s));
  Multiplexer multiplexer_1 (.in0(add_8bits_1_overflow), .in1(substractor_8bit_1_error), .out(Error), .sel(SlctOP[0]));
  Multiplexer #(.width(8)) multiplexer_2 (.in0(add_8bits_1_s), .in1(substractor_8bit_1_s), .out(S), .sel(SlctOP[0]));
endmodule

module Comparator_Operation_8bit (
  input  [7:0] A,
  input  [7:0] B,
  input  [3:0] SlctOP,
  output S
);

  wire different_operateur_8bit_1_s, equal_comparator_8bit_1_s, inferior_operator_8bit_1_s,
       superior_operator_8bit_1_s;

  Equal_Comparator_8bit equal_comparator_8bit_1 (.A(A), .B(B), .S(equal_comparator_8bit_1_s));
  Different_Operateur_8bit different_operateur_8bit_1 (.A(A), .B(B), .S(different_operateur_8bit_1_s));
  Superior_Operator_8bit superior_operator_8bit_1 (.A(A), .B(B), .S(superior_operator_8bit_1_s));
  Inferior_Operator_8bit inferior_operator_8bit_1 (.A(A), .B(B), .S(inferior_operator_8bit_1_s));
  Multiplexer #(.select(2)) multiplexer_1 (
    .in0(equal_comparator_8bit_1_s), .in1(different_operateur_8bit_1_s), .in2(superior_operator_8bit_1_s),
    .in3(inferior_operator_8bit_1_s), .out(S), .sel(SlctOP[1:0]));
endmodule

module Logic_Operation_8bit (
  input  [7:0] A,
  input  [7:0] B,
  input  [3:0] SlctOP,
  output [7:0] S
);

  wire [7:0] and_operator_8bit_1_s, or_operator_8bit_1_s, xor_operator_8bit_1_s;

  AND_Operator_8bit and_operator_8bit_1 (.A(A), .B(B), .S(and_operator_8bit_1_s));
  OR_Operator_8bit or_operator_8bit_1 (.A(A), .B(B), .S(or_operator_8bit_1_s));
  XOR_Operator_8bit xor_operator_8bit_1 (.A(A), .B(B), .S(xor_operator_8bit_1_s));
  Multiplexer #(.select(2), .width(8)) multiplexer_1 (
    .in0(and_operator_8bit_1_s), .in1(or_operator_8bit_1_s), .in2(xor_operator_8bit_1_s), .out(S),
    .sel(SlctOP[1:0]));  // open: in3
endmodule

module Offset_Rotation_8bit (
  input  [7:0] A,
  input  [3:0] SlctOP,
  output Error,
  output [7:0] S
);

  wire offsetleft_1_error, offsetright_1_error;
  wire [7:0] offsetleft_1_s, offsetright_1_s, rotationleft_1_s, rotationright_1_s;

  OffsetLeft offsetleft_1 (.A(A), .S(offsetleft_1_s), .Error(offsetleft_1_error));
  OffsetRight offsetright_1 (.A(A), .S(offsetright_1_s), .Error(offsetright_1_error));
  RotationLeft rotationleft_1 (.A(A), .S(rotationleft_1_s));
  RotationRight rotationright_1 (.A(A), .S(rotationright_1_s));
  Multiplexer multiplexer_1 (.in0(offsetleft_1_error), .in1(offsetright_1_error), .out(Error), .sel(SlctOP[0]));
  Multiplexer #(.select(2), .width(8)) multiplexer_2 (
    .in0(offsetleft_1_s), .in1(offsetright_1_s), .in2(rotationleft_1_s), .in3(rotationright_1_s), .out(S),
    .sel(SlctOP[1:0]));
endmodule
