// Logisim project AdderLib.circ as structural Verilog: 3 circuits, main circuit Add_1bit
module Add_1bit (
  input  A,
  input  B,
  output Value,
  output Carry
);

  wire not_1_out;

  xor xor_1 (Value, A, B);
  not not_1 (not_1_out, Value);
  and and_1 (Carry, not_1_out, A, B);
endmodule

module Add_3bit (
  input  A,
  input  B,
  input  Carry_In,
  output Value,
  output Carry_Out
);

  wire add_1bit_1_carry, add_1bit_1_value, add_1bit_2_carry;

  Add_1bit add_1bit_1 (.A(A), .B(B), .Value(add_1bit_1_value), .Carry(add_1bit_1_carry));
  Add_1bit add_1bit_2 (.A(add_1bit_1_value), .B(Carry_In), .Value(Value), .Carry(add_1bit_2_carry));
  or or_1 (Carry_Out, add_1bit_2_carry, add_1bit_1_carry);
endmodule

module Add_8bits (
  input  [7:0] A,
  input  [7:0] B,
  output [7:0] S,
  output Overflow
);

  wire add_1bit_1_carry, add_3bit_1_carry_out, add_3bit_2_carry_out, add_3bit_3_carry_out,
       add_3bit_4_carry_out, add_3bit_5_carry_out, add_3bit_6_carry_out;

  Add_1bit add_1bit_1 (.A(A[0]), .B(B[0]), .Value(S[0]), .Carry(add_1bit_1_carry));
  Add_3bit add_3bit_1 (.A(A[1]), .B(B[1]), .Carry_In(add_1bit_1_carry), .Value(S[1]), .Carry_Out(add_3bit_1_carry_out));
  Add_3bit add_3bit_2 (
    .A(A[2]), .B(B[2]), .Carry_In(add_3bit_1_carry_out), .Value(S[2]), .Carry_Out(add_3bit_2_carry_out));
  Add_3bit add_3bit_3 (
    .A(A[3]), .B(B[3]), .Carry_In(add_3bit_2_carry_out), .Value(S[3]), .Carry_Out(add_3bit_3_carry_out));
  Add_3bit add_3bit_4 (
    .A(A[4]), .B(B[4]), .Carry_In(add_3bit_3_carry_out), .Value(S[4]), .Carry_Out(add_3bit_4_carry_out));
  Add_3bit add_3bit_5 (
    .A(A[5]), .B(B[5]), .Carry_In(add_3bit_4_carry_out), .Value(S[5]), .Carry_Out(add_3bit_5_carry_out));
  Add_3bit add_3bit_6 (
    .A(A[6]), .B(B[6]), .Carry_In(add_3bit_5_carry_out), .Value(S[6]), .Carry_Out(add_3bit_6_carry_out));
  Add_3bit add_3bit_7 (.A(A[7]), .B(B[7]), .Carry_In(add_3bit_6_carry_out), .Value(S[7]), .Carry_Out(Overflow));
endmodule
