// Logisim project ArithmeticOperationLib.circ as structural Verilog: 5 circuits, main circuit substractor_8bit
module substractor_8bit (
  input  [7:0] A,
  input  [7:0] B,
  output Error,
  output [7:0] S
);

  wire add_8bit_1_overflow, and_2_out, complement_2_1_overflow, not_2_out;
  wire [7:0] and_1_out, complement_2_1_b_to_2, not_1_out;

  assign and_1_out = {8{1'b0}} & B;  // AND_Gate and_1, 8 bits wide
  assign not_1_out = ~and_1_out;  // NOT_Gate not_1, 8 bits wide
  complement_2 complement_2_1 (.B(B), .B_to_2(complement_2_1_b_to_2), .Overflow(complement_2_1_overflow));
  buf and_2 (and_2_out, complement_2_1_overflow);  // AND_Gate
  or or_1 (Error, and_2_out, not_2_out);
  not not_2 (not_2_out, add_8bit_1_overflow);
  Add_8bit add_8bit_1 (.A(A), .B(complement_2_1_b_to_2), .S(S), .Overflow(add_8bit_1_overflow));
endmodule

module complement_2 (
  input  [7:0] B,
  output [7:0] B_to_2,
  output Overflow
);

  wire [7:0] not_1_out;

  assign not_1_out = ~B;  // NOT_Gate not_1, 8 bits wide
  Add_8bit add_8bit_1 (.A(not_1_out), .B(8'h1), .S(B_to_2), .Overflow(Overflow));
endmodule

module Add_1bits (
  input  A,
  input  B,
  output Value,
  output Carry
);

  wire not_1_out;

  xor xor_1 (Value, A, B);
  not not_1 (not_1_out, Value);
  and and_1 (Carry, not_1_out, A, B);
endmodule

module Add_3bits (
  input  A,
  input  B,
  input  Carry_In,
  output Value,
  output Carry_Out
);

  wire add_1bits_1_carry, add_1bits_1_value, add_1bits_2_carry;

  Add_1bits add_1bits_1 (.A(A), .B(B), .Value(add_1bits_1_value), .Carry(add_1bits_1_carry));
  Add_1bits add_1bits_2 (.A(add_1bits_1_value), .B(Carry_In), .Value(Value), .Carry(add_1bits_2_carry));
  or or_1 (Carry_Out, add_1bits_2_carry, add_1bits_1_carry);
endmodule

module Add_8bit (
  input  [7:0] A,
  input  [7:0] B,
  output [7:0] S,
  output Overflow
);

  wire add_1bits_1_carry, add_3bits_1_carry_out, add_3bits_2_carry_out, add_3bits_3_carry_out,
       add_3bits_4_carry_out, add_3bits_5_carry_out, add_3bits_6_carry_out;

  Add_1bits add_1bits_1 (.A(A[0]), .B(B[0]), .Value(S[0]), .Carry(add_1bits_1_carry));
  Add_3bits add_3bits_1 (
    .A(A[1]), .B(B[1]), .Carry_In(add_1bits_1_carry), .Value(S[1]), .Carry_Out(add_3bits_1_carry_out));
  Add_3bits add_3bits_2 (
    .A(A[2]), .B(B[2]), .Carry_In(add_3bits_1_carry_out), .Value(S[2]), .Carry_Out(add_3bits_2_carry_out));
  Add_3bits add_3bits_3 (
    .A(A[3]), .B(B[3]), .Carry_In(add_3bits_2_carry_out), .Value(S[3]), .Carry_Out(add_3bits_3_carry_out));
  Add_3bits add_3bits_4 (
    .A(A[4]), .B(B[4]), .Carry_In(add_3bits_3_carry_out), .Value(S[4]), .Carry_Out(add_3bits_4_carry_out));
  Add_3bits add_3bits_5 (
    .A(A[5]), .B(B[5]), .Carry_In(add_3bits_4_carry_out), .Value(S[5]), .Carry_Out(add_3bits_5_carry_out));
  Add_3bits add_3bits_6 (
    .A(A[6]), .B(B[6]), .Carry_In(add_3bits_5_carry_out), .Value(S[6]), .Carry_Out(add_3bits_6_carry_out));
  Add_3bits add_3bits_7 (.A(A[7]), .B(B[7]), .Carry_In(add_3bits_6_carry_out), .Value(S[7]), .Carry_Out(Overflow));
endmodule
