// Logisim project ComparatorAndOperatorLib.circ as structural Verilog: 9 circuits, main circuit Equal_Comparator_8bit
module Equal_Comparator_8bit (
  input  [7:0] A,
  input  [7:0] B,
  output S
);

  wire [7:0] not_1_out, xor_operator_8bits_1_s;

  XOR_Operator_8bits xor_operator_8bits_1 (.A(A), .B(B), .S(xor_operator_8bits_1_s));
  assign not_1_out = ~xor_operator_8bits_1_s;  // NOT_Gate not_1, 8 bits wide
  and and_1 (S, not_1_out[0], not_1_out[1], not_1_out[2], not_1_out[3], not_1_out[4], not_1_out[5], not_1_out[6], not_1_out[7]);
endmodule

module Different_Operateur_8bit (
  input  [7:0] A,
  input  [7:0] B,
  output S
);

  wire equal_comparator_8bit_1_s;

  not not_1 (S, equal_comparator_8bit_1_s);
  Equal_Comparator_8bit equal_comparator_8bit_1 (.A(A), .B(B), .S(equal_comparator_8bit_1_s));
endmodule

module Inferior_Operator_8bit (
  input  [7:0] A,
  input  [7:0] B,
  output S
);

  wire and_1_out, and_2_out, and_3_out, and_4_out, and_5_out, and_6_out, and_7_out,
       inferior_operator_1bit_1_s, inferior_operator_1bit_2_s, inferior_operator_1bit_3_s,
       inferior_operator_1bit_4_s, inferior_operator_1bit_5_s, inferior_operator_1bit_6_s,
       inferior_operator_1bit_7_s, inferior_operator_1bit_8_s, not_1_out, not_2_out, not_3_out, not_4_out,
       not_5_out, not_6_out, not_7_out, xor_1_out, xor_2_out, xor_3_out, xor_4_out, xor_5_out, xor_6_out,
       xor_7_out;

  xor xor_1 (xor_1_out, A[7], B[7]);
  xor xor_2 (xor_2_out, A[6], B[6]);
  xor xor_3 (xor_3_out, A[5], B[5]);
  xor xor_4 (xor_4_out, A[4], B[4]);
  xor xor_5 (xor_5_out, A[3], B[3]);
  xor xor_6 (xor_6_out, A[2], B[2]);
  xor xor_7 (xor_7_out, A[1], B[1]);
  not not_1 (not_1_out, xor_1_out);
  not not_2 (not_2_out, xor_2_out);
  not not_3 (not_3_out, xor_3_out);
  not not_4 (not_4_out, xor_4_out);
  not not_5 (not_5_out, xor_5_out);
  not not_6 (not_6_out, xor_6_out);
  not not_7 (not_7_out, xor_7_out);
  Inferior_Operator_1bit inferior_operator_1bit_1 (.A(A[7]), .B(B[7]), .S(inferior_operator_1bit_1_s));
  Inferior_Operator_1bit inferior_operator_1bit_2 (.A(A[6]), .B(B[6]), .S(inferior_operator_1bit_2_s));
  Inferior_Operator_1bit inferior_operator_1bit_3 (.A(A[5]), .B(B[5]), .S(inferior_operator_1bit_3_s));
  Inferior_Operator_1bit inferior_operator_1bit_4 (.A(A[4]), .B(B[4]), .S(inferior_operator_1bit_4_s));
  Inferior_Operator_1bit inferior_operator_1bit_5 (.A(A[3]), .B(B[3]), .S(inferior_operator_1bit_5_s));
  Inferior_Operator_1bit inferior_operator_1bit_6 (.A(A[2]), .B(B[2]), .S(inferior_operator_1bit_6_s));
  Inferior_Operator_1bit inferior_operator_1bit_7 (.A(A[1]), .B(B[1]), .S(inferior_operator_1bit_7_s));
  Inferior_Operator_1bit inferior_operator_1bit_8 (.A(A[0]), .B(B[0]), .S(inferior_operator_1bit_8_s));
  and and_1 (and_1_out, not_1_out, inferior_operator_1bit_2_s);
  and and_2 (and_2_out, not_1_out, not_2_out, inferior_operator_1bit_3_s);
  and and_3 (and_3_out, not_2_out, not_3_out, inferior_operator_1bit_4_s);
  and and_4 (and_4_out, not_3_out, not_4_out, inferior_operator_1bit_5_s);
  and and_5 (and_5_out, not_4_out, not_5_out, inferior_operator_1bit_6_s);
  and and_6 (and_6_out, not_5_out, not_6_out, inferior_operator_1bit_7_s);
  and and_7 (and_7_out, not_6_out, not_7_out, inferior_operator_1bit_8_s);
  or or_1 (S, inferior_operator_1bit_1_s, and_1_out, and_2_out, and_3_out, and_4_out, and_5_out, and_6_out, and_7_out);
endmodule

module Inferior_Operator_1bit (
  input  A,
  input  B,
  output S
);

  wire and_1_out, nand_1_out;

  buf and_1 (and_1_out, B);  // AND_Gate
  not nand_1 (nand_1_out, A);  // NAND_Gate
  and and_2 (S, and_1_out, nand_1_out);
endmodule

module Superior_Operator_1bit (
  input  A,
  input  B,
  output S
);

  wire and_1_out, nand_1_out;

  not nand_1 (nand_1_out, B);  // NAND_Gate
  buf and_1 (and_1_out, A);  // AND_Gate
  and and_2 (S, nand_1_out, and_1_out);
endmodule

module Superior_Operator_8bit (
  input  [7:0] A,
  input  [7:0] B,
  output S
);

  wire and_1_out, and_2_out, and_3_out, and_4_out, and_5_out, and_6_out, and_7_out, not_1_out, not_2_out,
       not_3_out, not_4_out, not_5_out, not_6_out, not_7_out, superior_operator_1bit_1_s,
       superior_operator_1bit_2_s, superior_operator_1bit_3_s, superior_operator_1bit_4_s,
       superior_operator_1bit_5_s, superior_operator_1bit_6_s, superior_operator_1bit_7_s,
       superior_operator_1bit_8_s, xor_1_out, xor_2_out, xor_3_out, xor_4_out, xor_5_out, xor_6_out,
       xor_7_out;

  xor xor_1 (xor_1_out, A[7], B[7]);
  xor xor_2 (xor_2_out, A[6], B[6]);
  xor xor_3 (xor_3_out, A[5], B[5]);
  xor xor_4 (xor_4_out, A[4], B[4]);
  xor xor_5 (xor_5_out, A[3], B[3]);
  xor xor_6 (xor_6_out, A[2], B[2]);
  xor xor_7 (xor_7_out, A[1], B[1]);
  not not_1 (not_1_out, xor_1_out);
  not not_2 (not_2_out, xor_2_out);
  not not_3 (not_3_out, xor_3_out);
  not not_4 (not_4_out, xor_4_out);
  not not_5 (not_5_out, xor_5_out);
  not not_6 (not_6_out, xor_6_out);
  not not_7 (not_7_out, xor_7_out);
  Superior_Operator_1bit superior_operator_1bit_1 (.A(A[7]), .B(B[7]), .S(superior_operator_1bit_1_s));
  Superior_Operator_1bit superior_operator_1bit_2 (.A(A[6]), .B(B[6]), .S(superior_operator_1bit_2_s));
  Superior_Operator_1bit superior_operator_1bit_3 (.A(A[5]), .B(B[5]), .S(superior_operator_1bit_3_s));
  Superior_Operator_1bit superior_operator_1bit_4 (.A(A[4]), .B(B[4]), .S(superior_operator_1bit_4_s));
  Superior_Operator_1bit superior_operator_1bit_5 (.A(A[3]), .B(B[3]), .S(superior_operator_1bit_5_s));
  Superior_Operator_1bit superior_operator_1bit_6 (.A(A[2]), .B(B[2]), .S(superior_operator_1bit_6_s));
  Superior_Operator_1bit superior_operator_1bit_7 (.A(A[1]), .B(B[1]), .S(superior_operator_1bit_7_s));
  Superior_Operator_1bit superior_operator_1bit_8 (.A(A[0]), .B(B[0]), .S(superior_operator_1bit_8_s));
  and and_1 (and_1_out, not_1_out, superior_operator_1bit_2_s);
  and and_2 (and_2_out, not_1_out, not_2_out, superior_operator_1bit_3_s);
  and and_3 (and_3_out, not_2_out, not_3_out, superior_operator_1bit_4_s);
  and and_4 (and_4_out, not_3_out, not_4_out, superior_operator_1bit_5_s);
  and and_5 (and_5_out, not_4_out, not_5_out, superior_operator_1bit_6_s);
  and and_6 (and_6_out, not_5_out, not_6_out, superior_operator_1bit_7_s);
  and and_7 (and_7_out, not_6_out, not_7_out, superior_operator_1bit_8_s);
  or or_1 (S, superior_operator_1bit_1_s, and_1_out, and_2_out, and_3_out, and_4_out, and_5_out, and_6_out, and_7_out);
endmodule

module AND_Operator_8bits (
  input  [7:0] A,
  input  [7:0] B,
  output [7:0] S
);

  and and_1 (S[0], A[0], B[0]);
  and and_2 (S[1], A[1], B[1]);
  and and_3 (S[2], A[2], B[2]);
  and and_4 (S[3], A[3], B[3]);
  and and_5 (S[4], A[4], B[4]);
  and and_6 (S[5], A[5], B[5]);
  and and_7 (S[6], A[6], B[6]);
  and and_8 (S[7], A[7], B[7]);
endmodule

module OR_Operator_8bits (
  input  [7:0] A,
  input  [7:0] B,
  output [7:0] S
);

  or or_1 (S[0], A[0], B[0]);
  or or_2 (S[1], A[1], B[1]);
  or or_3 (S[2], A[2], B[2]);
  or or_4 (S[3], A[3], B[3]);
  or or_5 (S[4], A[4], B[4]);
  or or_6 (S[5], A[5], B[5]);
  or or_7 (S[6], A[6], B[6]);
  or or_8 (S[7], A[7], B[7]);
endmodule

module XOR_Operator_8bits (
  input  [7:0] A,
  input  [7:0] B,
  output [7:0] S
);

  xor xor_1 (S[0], A[0], B[0]);
  xor xor_2 (S[1], A[1], B[1]);
  xor xor_3 (S[2], A[2], B[2]);
  xor xor_4 (S[3], A[3], B[3]);
  xor xor_5 (S[4], A[4], B[4]);
  xor xor_6 (S[5], A[5], B[5]);
  xor xor_7 (S[6], A[6], B[6]);
  xor xor_8 (S[7], A[7], B[7]);
endmodule
