// Logisim project CyProcessingUnit.circ as structural Verilog: 7 circuits, main circuit main
module main (
  input  in_1,
  output [7:0] C
);

  wire alu_1_p4, decoder_operation_1_store, registerband_8bit_1_s_1bit;
  wire [1:0] decoder_operation_1_jump, decoder_operation_1_select_reg_in;
  wire [3:0] decoder_operation_1_s, decoders_1_rin1, decoders_1_rin2, decoders_1_rout, undriven_2,
       undriven_3, undriven_5, undriven_6, undriven_7;
  wire [7:0] A, B, COde, Data, decoders_1_addr8, decoders_1_operation, ip_1_adrr_data, ip_1_reg_in;
  wire [11:0] undriven_4;
  wire [23:0] decoders_1_decoder_24bit, fetch_1_a2, ram_instruction_1_a2, undriven;

  Hex_Digit_Display hex_digit_display_1 (.value(undriven_3));  // open: dp
  Hex_Digit_Display hex_digit_display_2 (.value(undriven[23:20]));  // open: dp
  Hex_Digit_Display hex_digit_display_3 (.value(COde[7:4]));  // open: dp
  Clock clock_1 ();  // open: out
  Hex_Digit_Display hex_digit_display_4 (.value(undriven_2));  // open: dp
  Hex_Digit_Display hex_digit_display_5 (.value(COde[3:0]));  // open: dp
  RAM_data ram_data_1 (
    .STORE(decoder_operation_1_store), .SELECTOR(ip_1_adrr_data), .INPUT_DATA(A), .OUTPUT_DATA(Data));
  RAM_Instruction ram_instruction_1 (.Memory_Choice(COde), .A2(ram_instruction_1_a2));
  Hex_Digit_Display hex_digit_display_6 (.value(undriven[11:8]));  // open: dp
  Hex_Digit_Display hex_digit_display_7 (.value(undriven[7:4]));  // open: dp
  Hex_Digit_Display hex_digit_display_8 (.value(undriven[3:0]));  // open: dp
  LED led_1 (.in(registerband_8bit_1_s_1bit));
  Hex_Digit_Display hex_digit_display_9 (.value(undriven_7));  // open: dp
  Fetch fetch_1 (.A1(ram_instruction_1_a2), .JUMP(decoder_operation_1_jump), .A2(fetch_1_a2));
  Hex_Digit_Display hex_digit_display_10 (.value(undriven_6));  // open: dp
  Hex_Digit_Display hex_digit_display_11 (.value(undriven_5));  // open: dp
  Hex_Digit_Display hex_digit_display_12 (.value(undriven_4[11:8]));  // open: dp
  Hex_Digit_Display hex_digit_display_13 (.value(undriven_4[7:4]));  // open: dp
  Decoders decoders_1 (
    .A(fetch_1_a2), .Rout(decoders_1_rout), .Rin2(decoders_1_rin2), .Rin1(decoders_1_rin1),
    .Operation(decoders_1_operation[3:0]), .Type_Op(decoders_1_operation[7:4]), .ADDR8(decoders_1_addr8),
    .Decoder_24bit(decoders_1_decoder_24bit));  // open: Unused
  Hex_Digit_Display hex_digit_display_14 (.value(undriven_4[3:0]));  // open: dp
  Hex_Digit_Display hex_digit_display_15 (.value(Data[7:4]));  // open: dp
  Hex_Digit_Display hex_digit_display_16 (.value(Data[3:0]));  // open: dp
  Hex_Digit_Display hex_digit_display_17 (.value(A[3:0]));  // open: dp
  Hex_Digit_Display hex_digit_display_18 (.value(A[7:4]));  // open: dp
  Hex_Digit_Display hex_digit_display_19 (.value(B[7:4]));  // open: dp
  Hex_Digit_Display hex_digit_display_20 (.value(B[3:0]));  // open: dp
  IP ip_1 (
    .Jump(decoder_operation_1_jump), .ALU(C), .RAM(Data), .ADDR8(decoders_1_addr8),
    .LOAD(decoder_operation_1_select_reg_in), .Kill(in_1), .REG_IN(ip_1_reg_in), .ADRR_DATA(ip_1_adrr_data),
    .ADDR_CODE(COde));
  Decoder_Operation decoder_operation_1 (
    .A(decoders_1_operation), .Flag(registerband_8bit_1_s_1bit), .S(decoder_operation_1_s),
    .SELECT_REG_IN(decoder_operation_1_select_reg_in), .STORE(decoder_operation_1_store),
    .JUMP(decoder_operation_1_jump));
  RegisterBand_8bit registerband_8bit_1 (
    .SlctC(decoders_1_rout), .Data(ip_1_reg_in), .SlctA(decoders_1_rin1[2:0]), .SlctB(decoders_1_rin2[2:0]),
    .S_1bit(registerband_8bit_1_s_1bit), .A(A), .B(B));
  LED led_2 (.in(alu_1_p4));
  // ALU alu_1: pin names not known; wires that end beside it: A, B, decoder_operation_1_s, alu_1_p4, C
endmodule

module Decoder_Operation (
  input  [7:0] A,
  input  Flag,
  output [3:0] S,
  output [1:0] SELECT_REG_IN,
  output STORE,
  output [1:0] JUMP
);

  wire not_1_out, not_2_out, not_3_out, not_4_out, not_5_out, not_6_out, not_7_out, not_8_out, not_9_out,
       or_1_out, or_2_out, or_3_out, or_4_out, or_5_out, or_6_out, or_7_out, or_8_out, or_9_out, or_10_out,
       or_11_out, or_12_out, or_13_out, or_14_out, or_15_out, or_16_out, or_17_out, or_18_out, or_19_out,
       or_20_out, or_21_out, or_22_out, or_23_out;

  not not_1 (not_1_out, A[7]);
  not not_2 (not_2_out, A[6]);
  not not_3 (not_3_out, A[5]);
  not not_4 (not_4_out, A[4]);
  not not_5 (not_5_out, A[3]);
  not not_6 (not_6_out, A[2]);
  not not_7 (not_7_out, A[1]);
  not not_8 (not_8_out, A[0]);
  not not_9 (not_9_out, Flag);
  or or_1 (or_1_out, A[4], A[3]);
  or or_2 (or_2_out, not_4_out, not_5_out);
  or or_3 (or_3_out, A[7], A[6], A[5], A[3], A[2], A[1], A[0]);
  or or_4 (or_4_out, A[4], not_7_out);
  or or_5 (or_5_out, not_4_out, A[1]);
  or or_6 (or_6_out, A[7], A[6], A[5], A[2], A[1], A[0]);
  or or_7 (or_7_out, A[4], A[2]);
  or or_8 (or_8_out, A[2], A[0]);
  or or_9 (or_9_out, A[2], A[0]);
  or or_10 (or_10_out, not_6_out, not_8_out);
  or or_11 (or_11_out, A[4], A[2], A[0]);
  or or_12 (or_12_out, not_6_out, not_7_out, not_8_out);
  or or_13 (or_13_out, not_5_out, not_7_out);
  or or_14 (or_14_out, not_5_out, not_6_out);
  or or_15 (or_15_out, not_4_out, not_7_out, not_8_out);
  or or_16 (or_16_out, not_4_out, not_6_out);
  or or_17 (or_17_out, not_3_out, not_8_out);
  or or_18 (or_18_out, not_3_out, not_7_out);
  or or_19 (or_19_out, not_3_out, A[2]);
  or or_20 (or_20_out, A[5], A[4], A[1], A[0]);
  and and_1 (STORE, A[5], A[1], not_8_out, not_6_out, not_5_out, not_4_out, not_2_out, not_1_out);
  or or_21 (or_21_out, A[0], not_9_out);
  or or_22 (or_22_out, not_8_out, Flag);
  or or_23 (or_23_out, not_7_out, Flag);
  and and_2 (S[3], or_1_out, or_2_out);
  and and_3 (S[2], or_3_out, not_4_out);
  and and_4 (S[1], or_4_out, not_5_out, or_5_out, or_6_out);
  and and_5 (S[0], or_7_out, or_8_out);
  and and_6 (SELECT_REG_IN[1], A[5], or_9_out, not_7_out, or_10_out, not_5_out, not_4_out, not_2_out, not_1_out);
  and and_7 (SELECT_REG_IN[0], or_11_out, or_12_out, or_13_out, or_14_out, or_15_out, or_16_out, or_17_out, or_18_out, not_2_out, not_1_out, or_19_out, or_20_out);
  and and_8 (JUMP[1], A[5], A[2], A[1], or_21_out, or_22_out, not_5_out, not_4_out, not_2_out, not_1_out);
  and and_9 (JUMP[0], A[5], A[2], A[0], or_23_out, not_5_out, not_4_out, not_2_out, not_1_out);
endmodule

module Fetch (
  input  [23:0] A1,
  input  [1:0] JUMP,
  output [23:0] A2
);

  wire [23:0] register_24bit_1_out_3;

  Register_24bit register_24bit_1 (.in_1(A1), .WE(1'b1), .out_3(register_24bit_1_out_3));
  Multiplexer #(.select(2), .width(24)) multiplexer_1 (
    .in0(register_24bit_1_out_3), .in1({24{1'b0}}), .in2({24{1'b0}}), .in3({24{1'b0}}), .out(A2), .sel(JUMP));
endmodule

module RAM_Instruction (
  input  [7:0] Memory_Choice,
  output [23:0] A2
);

  ROM #(.dataWidth(24)) rom_1 (.addr(Memory_Choice), .data(A2));

  // Notes on the sheet:
  //   contents of rom_1 (hex, n*v repeats v):
  //   0 0 240030 240031 240002 240003 240014 13107 2600e0 182002 183403 250060 9*222000
endmodule

module RAM_data (
  input  [7:0] SELECTOR,
  input  STORE,
  input  [7:0] INPUT_DATA,
  output [7:0] OUTPUT_DATA
);

  wire clock_1_out;

  RAM #(.asyncread("true")) ram_1 (
    .addr(SELECTOR), .we(STORE), .clk(clock_1_out), .din(INPUT_DATA), .dout(OUTPUT_DATA));  // open: oe
  Clock clock_1 (.out(clock_1_out));
endmodule

module Decoders (
  input  [23:0] A,
  output [23:0] Decoder_24bit,
  output [3:0] Rout,
  output [7:0] ADDR8,
  output [3:0] Unused,
  output [3:0] Rin2,
  output [3:0] Rin1,
  output [3:0] Operation,
  output [3:0] Type_Op
);

  Register_24bit register_24bit_1 (.in_1(A), .WE(1'b1), .out_3({Decoder_24bit[23:12], ADDR8, Decoder_24bit[3:0]}));

  assign Decoder_24bit[11:4] = ADDR8;
  assign Operation = Decoder_24bit[19:16];
  assign Rin1 = Decoder_24bit[15:12];
  assign Rin2 = ADDR8[7:4];
  assign Rout = Decoder_24bit[3:0];
  assign Type_Op = Decoder_24bit[23:20];
  assign Unused = ADDR8[3:0];
endmodule

module IP (
  input  [7:0] ALU,
  input  [7:0] RAM,
  input  [7:0] ADDR8,
  input  [1:0] LOAD,
  input  Kill,
  input  [1:0] Jump,
  output [7:0] REG_IN,
  output [7:0] ADRR_DATA,
  output [7:0] ADDR_CODE
);

  wire [7:0] adder_1_out, multiplexer_1_out, multiplexer_2_out;

  Multiplexer #(.select(2), .width(8)) multiplexer_1 (
    .in0(multiplexer_2_out), .in1(ADDR8), .in2(ADDR8), .in3(ADDR8), .out(multiplexer_1_out), .sel(Jump));
  Register_8bit register_8bit_1 (.in_1(multiplexer_1_out), .WE(1'b1), .out_3(ADDR_CODE));
  Adder adder_1 (.a(8'h1), .b(ADDR_CODE), .out(adder_1_out));  // open: cin, cout
  Multiplexer #(.width(8)) multiplexer_2 (.in0(adder_1_out), .in1({8{1'b0}}), .out(multiplexer_2_out), .sel(Kill));
  Multiplexer #(.select(2), .width(8)) multiplexer_3 (
    .in1(ALU), .in2(RAM), .in3(ADDR8), .out(REG_IN), .sel(LOAD));  // open: in0

  assign ADRR_DATA = ADDR8;
endmodule
