// Logisim project OffsetAndRotationLib.circ as structural Verilog: 5 circuits, main circuit OffsetLeft
module OffsetLeft (
  input  [7:0] A,
  output [7:0] S,
  output Error
);


  assign Error = A[7];
  assign S = {A[6:0], 1'b0};
endmodule

module OffsetRight (
  input  [7:0] A,
  output [7:0] S,
  output Error
);


  assign Error = A[0];
  assign S = {1'b0, A[7:1]};
endmodule

module RotationLeft (
  input  [7:0] A,
  output [7:0] S
);


  assign S = {A[6:0], A[7]};
endmodule

module RotationRight (
  input  [7:0] A,
  output [7:0] S
);


  assign S = {A[0], A[7:1]};
endmodule

module ASR (
  input  [7:0] A,
  output [7:0] S,
  output Error
);


  assign Error = A[0];
  assign S = {{2{A[7]}}, A[6:1]};
endmodule
