// Logisim project RegisterLib.circ as structural Verilog: 4 circuits, main circuit Register_8bit
module Register_8bit (
  input  [7:0] in_1,
  input  WE,
  output [7:0] out_3
);

  wire clock_1_out;
  wire [7:0] multiplexer_1_out;

  Multiplexer #(.width(8)) multiplexer_1 (.in0(out_3), .in1(in_1), .out(multiplexer_1_out), .sel(WE));
  Clock clock_1 (.out(clock_1_out));
  D_Flip_Flop d_ff_1 (.D(multiplexer_1_out[0]), .clk(clock_1_out), .Q(out_3[0]));  // open: Qn, preset, reset
  D_Flip_Flop d_ff_2 (.D(multiplexer_1_out[1]), .clk(clock_1_out), .Q(out_3[1]));  // open: Qn, preset, reset
  D_Flip_Flop d_ff_3 (.D(multiplexer_1_out[2]), .clk(clock_1_out), .Q(out_3[2]));  // open: Qn, preset, reset
  D_Flip_Flop d_ff_4 (.D(multiplexer_1_out[3]), .clk(clock_1_out), .Q(out_3[3]));  // open: Qn, preset, reset
  D_Flip_Flop d_ff_5 (.D(multiplexer_1_out[4]), .clk(clock_1_out), .Q(out_3[4]));  // open: Qn, preset, reset
  D_Flip_Flop d_ff_6 (.D(multiplexer_1_out[5]), .clk(clock_1_out), .Q(out_3[5]));  // open: Qn, preset, reset
  D_Flip_Flop d_ff_7 (.D(multiplexer_1_out[6]), .clk(clock_1_out), .Q(out_3[6]));  // open: Qn, preset, reset
  D_Flip_Flop d_ff_8 (.D(multiplexer_1_out[7]), .clk(clock_1_out), .Q(out_3[7]));  // open: Qn, preset, reset
endmodule

module RegisterBand_8bit (
  input  [7:0] Data,
  input  [2:0] SlctA,
  input  [2:0] SlctB,
  input  [3:0] SlctC,
  output [7:0] A,
  output [7:0] B,
  output S_1bit
);

  wire decoder_1_out0, decoder_1_out1, decoder_1_out2, decoder_1_out3, decoder_1_out4, decoder_1_out5,
       decoder_1_out6, decoder_1_out7;
  wire [7:0] register_8bit_1_out_3, register_8bit_2_out_3, register_8bit_3_out_3, register_8bit_4_out_3,
       register_8bit_5_out_3, register_8bit_6_out_3, register_8bit_7_out_3;
  wire [7:1] register_1bit_1_out_3;

  Decoder #(.enable("false"), .select(4)) decoder_1 (
    .out0(decoder_1_out0), .out1(decoder_1_out1), .out2(decoder_1_out2), .out3(decoder_1_out3),
    .out4(decoder_1_out4), .out5(decoder_1_out5), .out6(decoder_1_out6), .out7(decoder_1_out7), .sel(SlctC));  // open: out8, out9, out10, out11, out12, out13, out14, out15
  Register_8bit register_8bit_1 (.in_1(Data), .WE(decoder_1_out0), .out_3(register_8bit_1_out_3));
  Register_8bit register_8bit_2 (.in_1(Data), .WE(decoder_1_out1), .out_3(register_8bit_2_out_3));
  Register_8bit register_8bit_3 (.in_1(Data), .WE(decoder_1_out2), .out_3(register_8bit_3_out_3));
  Register_8bit register_8bit_4 (.in_1(Data), .WE(decoder_1_out3), .out_3(register_8bit_4_out_3));
  Register_8bit register_8bit_5 (.in_1(Data), .WE(decoder_1_out4), .out_3(register_8bit_5_out_3));
  Register_8bit register_8bit_6 (.in_1(Data), .WE(decoder_1_out5), .out_3(register_8bit_6_out_3));
  Register_8bit register_8bit_7 (.in_1(Data), .WE(decoder_1_out6), .out_3(register_8bit_7_out_3));
  Register_1bit register_1bit_1 (.in_1(Data), .WE(decoder_1_out7), .out_3({register_1bit_1_out_3, S_1bit}));
  Multiplexer #(.select(3), .width(8)) multiplexer_1 (
    .in0(register_8bit_1_out_3), .in1(register_8bit_2_out_3), .in2(register_8bit_3_out_3),
    .in3(register_8bit_4_out_3), .in4(register_8bit_5_out_3), .in5(register_8bit_6_out_3),
    .in6(register_8bit_7_out_3), .in7({register_1bit_1_out_3, S_1bit}), .out(A), .sel(SlctA));
  Multiplexer #(.select(3), .width(8)) multiplexer_2 (
    .in0(register_8bit_1_out_3), .in1(register_8bit_2_out_3), .in2(register_8bit_3_out_3),
    .in3(register_8bit_4_out_3), .in4(register_8bit_5_out_3), .in5(register_8bit_6_out_3),
    .in6(register_8bit_7_out_3), .in7({register_1bit_1_out_3, S_1bit}), .out(B), .sel(SlctB));
endmodule

module Register_1bit (
  input  [7:0] in_1,
  input  WE,
  output [7:0] out_3
);

  wire clock_1_out, d_ff_1_q, multiplexer_1_out;

  Multiplexer multiplexer_1 (.in0(d_ff_1_q), .in1(in_1[0]), .out(multiplexer_1_out), .sel(WE));
  Clock clock_1 (.out(clock_1_out));
  D_Flip_Flop d_ff_1 (.D(multiplexer_1_out), .clk(clock_1_out), .Q(d_ff_1_q));  // open: Qn, preset, reset
  assign out_3 = {{7{1'b0}}, d_ff_1_q};  // Bit_Extender bit_extender_1
endmodule

module Register_24bit (
  input  [23:0] in_1,
  input  WE,
  output [23:0] out_3
);

  Register_8bit register_8bit_1 (.in_1(in_1[7:0]), .WE(WE), .out_3(out_3[7:0]));
  Register_8bit register_8bit_2 (.in_1(in_1[15:8]), .WE(WE), .out_3(out_3[15:8]));
  Register_8bit register_8bit_3 (.in_1(in_1[23:16]), .WE(WE), .out_3(out_3[23:16]));
endmodule
